# Fritzing sketch BluetoothLed (saved by Fritzing 0.8.7b)
breadboards: 1

parts:
  Part1 = Arduino Uno (Rev3)
  LED1 = RGB LED (com. cathode, rgb) [package="5 mm [THT]"]
  R1 = Resistor [tolerance=±5% resistance=330 package=THT]
  R2 = Resistor [tolerance=±5% resistance=330 package=THT]
  R3 = Resistor [tolerance=±5% resistance=330 package=THT]
  Part2 = Bluetooth Mate Silver [part_number="JY-MCU,HC-06(3.3V RX/TX)"]
  R4 = Resistor [tolerance=±5% resistance=10k package=THT]
  R5 = Resistor [tolerance=±5% resistance=10k package=THT]
  R6 = Resistor [tolerance=±5% resistance=10k package=THT]

nets:
  N1: Part1.D9_PWM, R3.Pin_1
  N2: Part1.D10_PWM/SS, R2.Pin_1
  N3: Part1.D11_PWM/MOSI, R1.Pin_1
  N4: Part1.D0/RX, Part2.TX_5V
  N5: Part1.D1/TX, R4.Pin_0
  5V: Part1.5V, Part2.VCC
  N6: LED1.red_anode, R1.Pin_0
  N7: LED1.common_cathode, Part2.GND, R5.Pin_1
  N8: LED1.green_anode, R2.Pin_0
  N9: LED1.blue_anode, R3.Pin_0
  N10: Part2.RX_5V, R4.Pin_1, R6.Pin_0
  N11: R5.Pin_0, R6.Pin_1
